# Fritzing sketch 4-bit_ALU (saved by Fritzing 0.9.3b)
breadboards: 3

parts:
  U1 = 7427 3 x 3 Input NOR Gate [part_number=7427 package="DIP (Dual Inline) [THT]"]
  U2 = 7474 Dual Positive Edge Triggered D Flip Flop [part_number=7474 package="DIP (Dual Inline) [THT]"]
  U3 = 74161 4 Bit Synchronous Up Down Counter [part_number=74161 package="DIP16 [THT]"]
  S1 = Pushbutton [package="[SMD]"]
  R1 = Resistor [tolerance=±5% resistance=220 package=THT]
  R2 = Resistor [tolerance=±5% resistance=220 package=THT]
  R3 = Resistor [tolerance=±5% resistance=220 package=THT]
  R4 = Resistor [tolerance=±5% resistance=220 package=THT]
  R5 = Resistor [tolerance=±5% resistance=220 package=THT]
  R6 = Resistor [tolerance=±5% resistance=220 package=THT]
  U4 = 74153 Dual 4:1 MUX [part_number=74153 package="DIP16 [THT]"]  # not connected
  U5 = 7400 4 x 2 Input NAND Gate [part_number=7400 package="DIP (Dual Inline) [THT]"]  # not connected
  U6 = 7486 4 x 2 Input XOR Gate [part_number=7486 package="DIP (Dual Inline) [THT]"]  # not connected
  U7 = 74153 Dual 4:1 MUX [part_number=74153 package="DIP16 [THT]"]  # not connected

nets:
  N1: U1.A1, R2.Pin_1
  GND: U1.GND, U2.GND, U3.GND, R2.Pin_0
  VDD: U1.VDD, U2.VDD, U3.VCC, R1.Pin_1, R5.Pin_1, R6.Pin_1
  N2: U2.A1, R3.Pin_1
  N3: U2.Q2, R4.Pin_1
  N4: U2.Q3, R6.Pin_0
  N5: U2.B4, R5.Pin_0
  N6: U3.7, U3.9, U3.10, R1.Pin_0
  N7: S1.Pin_1, S1.Pin_2
  N8: S1.Pin_3, S1.Pin_4
  N9: R3.Pin_0, R4.Pin_0

notes:
  Compute Unit:
  x1 4:1 MUX
  x3 2 Input XOR
  x4 2 Input NAND
  ----------------------
  Extra:
  x1 4:1 MUX
  x1 2 Input XOR
  *** 3 Chips ***
  Routing Unit:
  x2 4:1 MUX
  ----------------------
  Extra:
  *** 1 Chip ***
  Register Unit:
  x2 Shift Registers
  x4 2 Input NAND
  x2 2 Input XOR
  --------------------------
  Extra:
  *** 4 Chips ***
  Control Unit:
  x1 Counter
  x3 Triple Input NOR
  --------------------------
  Extra:
  *** 2 Chips ***
  Flip -Flops
  --------------
  Right: Q
  Left: S

custom parts:
  7427 3 x 3 Input NOR Gate: 7427 3 x 2 Input NOR Gate
  74153 Dual 4:1 MUX: 74153 Dual 4:1 Multiplexor
